# Fritzing sketch Tach (saved by Fritzing 0.9.3b)
circuit board: 8.46667cm x 5.64444cm
breadboards: 1

parts:
  R1 = Resistor [tolerance=±5% resistance=470 package=THT]
  R2 = Resistor [tolerance=±5% resistance=220 package=THT]
  Part1 = Arduino Pro Mini v13
  Q1 = NPN-Transistor [part_number=2N3904 package="TO92 [THT]"]
  R4 = Resistor [tolerance=±5% resistance=10k package=THT]
  U1 = Voltage Regulator - 5V [part_number=L7905 package="TO220 [THT]"]
  J1 = female pin header, 3 pins [form="♀ (female)"]
  J2 = male pin header, 3 pins [form="♂ (male)"]
  Q2 = NPN-Transistor [part_number="3144 Hall Effect Sensor" package="TO92 [THT]"]
  U2 = MAGNET [package=magnet-18mm]  # not connected
  U3 = mystery part, 2 pins [chip_label=Galvanometer]
  R3 = Resistor [tolerance=±5% resistance=22 package=THT]

nets:
  N1: R1.Pin_0, Part1.VCC, R4.Pin_1, U1.output_voltage, J1.pin1
  N2: R1.Pin_1, R2.Pin_0
  N3: R2.Pin_1, U3.pin1, R3.Pin_1
  GND: Part1.GND, U1.GND, J1.pin2, R3.Pin_0
  N4: Part1.D2, R4.Pin_0, J1.pin3
  N5: Q1.C, U3.pin2
  N6: J2.pin1, Q2.E
  N7: J2.pin2, Q2.B
  N8: J2.pin3, Q2.C

custom parts:
  MAGNET: Ceramic disc magnet, COM-08890
